# Fritzing sketch servo_board (saved by Fritzing 0.7.10b)
stripboards: 1

parts:
  J1 = female pin header, 1 pin [form="♀ (female)"]  # not connected
  J3 = male pin header, 8 pins [form="♂ (male)"]  # not connected
  J2 = male pin header, 8 pins [form="♂ (male)"]
  U1 = atmega168 [package=dip]
  U2 = mystery part, 3 pins [chip_label="IR receiver"]
  J4 = female pin header, 3 pins [form="♀ (female)"]

nets:
  N1: J2.pin4, U1.GND#21
  N2: J2.pin6, U1.A5
  N3: J2.pin7, U1.A4
  N4: J2.pin8, U1.AVCC
  N5: U1.D1_(TX), U2.pin1, J4.pin1
  N6: U1.VCC, U2.pin3, J4.pin3
  N7: U1.GND#7, U2.pin2, J4.pin2
